# Fritzing sketch Esquematico Ariyuu (saved by Fritzing 1.0.6)
circuit board: 8.46667cm x 5.64444cm
breadboards: 1

parts:
  J1 = Basic Servo
  Lipo_1s = LIPO-2200mAh
  Mod1 = 2S-BMS
  Lipo_1s_2 = LIPO-2200mAh
  Lipo_1s_3 = LIPO-2200mAh
  Lipo_1s_4 = LIPO-2200mAh
  Mod2 = 2S-BMS
  esp1 = ESP32 DevKitc V4
  Buck_Convertor1 = Buck Convertor [part_number=LM2596 package=THT]
  Componente1 = Adafruit PCA9685 PWM/Servo Breakout [part_number=815]
  U1 = Sharp PC817 [package=THT]
  R1 = Resistor [tolerance=±5% power=0.25W resistance=220 package=THT]
  R2 = Resistor [tolerance=±5% power=0.25W resistance=1k package=THT]
  U2 = Sharp PC817 [package=THT]
  R3 = Resistor [tolerance=±5% power=0.25W resistance=220 package=THT]
  R4 = Resistor [tolerance=±5% power=0.25W resistance=1k package=THT]
  U3 = Sharp PC817 [package=THT]
  U4 = Sharp PC817 [package=THT]
  R5 = Resistor [tolerance=±5% power=0.25W resistance=220 package=THT]
  R6 = Resistor [tolerance=±5% power=0.25W resistance=220 package=THT]
  R7 = Resistor [tolerance=±5% power=0.25W resistance=1k package=THT]
  R8 = Resistor [tolerance=±5% power=0.25W resistance=1k package=THT]
  U5 = Sharp PC817 [package=THT]
  U6 = Sharp PC817 [package=THT]
  U7 = Sharp PC817 [package=THT]
  U8 = Sharp PC817 [package=THT]
  R9 = Resistor [tolerance=±5% power=0.25W resistance=220 package=THT]
  R10 = Resistor [tolerance=±5% power=0.25W resistance=220 package=THT]
  R11 = Resistor [tolerance=±5% power=0.25W resistance=220 package=THT]
  R12 = Resistor [tolerance=±5% power=0.25W resistance=220 package=THT]
  R13 = Resistor [tolerance=±5% power=0.25W resistance=1k package=THT]
  R14 = Resistor [tolerance=±5% power=0.25W resistance=1k package=THT]
  R15 = Resistor [tolerance=±5% power=0.25W resistance=1k package=THT]
  R16 = Resistor [tolerance=±5% power=0.25W resistance=1k package=THT]
  U9 = Sharp PC817 [package=THT]
  U10 = Sharp PC817 [package=THT]
  U11 = Sharp PC817 [package=THT]
  U12 = Sharp PC817 [package=THT]
  R17 = Resistor [tolerance=±5% power=0.25W resistance=220 package=THT]
  R18 = Resistor [tolerance=±5% power=0.25W resistance=220 package=THT]
  R19 = Resistor [tolerance=±5% power=0.25W resistance=220 package=THT]
  R20 = Resistor [tolerance=±5% power=0.25W resistance=220 package=THT]
  R21 = Resistor [tolerance=±5% power=0.25W resistance=1k package=THT]
  R22 = Resistor [tolerance=±5% power=0.25W resistance=1k package=THT]
  R23 = Resistor [tolerance=±5% power=0.25W resistance=1k package=THT]
  R24 = Resistor [tolerance=±5% power=0.25W resistance=1k package=THT]
  U13 = Sharp PC817 [package=THT]
  U14 = Sharp PC817 [package=THT]
  U15 = Sharp PC817 [package=THT]
  U16 = Sharp PC817 [package=THT]
  R25 = Resistor [tolerance=±5% power=0.25W resistance=220 package=THT]
  R26 = Resistor [tolerance=±5% power=0.25W resistance=220 package=THT]
  R27 = Resistor [tolerance=±5% power=0.25W resistance=220 package=THT]
  R28 = Resistor [tolerance=±5% power=0.25W resistance=220 package=THT]
  R29 = Resistor [tolerance=±5% power=0.25W resistance=1k package=THT]
  R30 = Resistor [tolerance=±5% power=0.25W resistance=1k package=THT]
  R31 = Resistor [tolerance=±5% power=0.25W resistance=1k package=THT]
  R32 = Resistor [tolerance=±5% power=0.25W resistance=1k package=THT]
  J2 = Basic Servo
  J3 = Basic Servo
  J4 = Basic Servo
  J5 = Basic Servo
  J6 = Basic Servo
  J7 = Basic Servo
  J8 = Basic Servo
  J9 = Basic Servo
  J10 = Basic Servo
  J11 = Basic Servo
  J12 = Basic Servo
  J13 = Basic Servo
  J14 = Basic Servo
  J15 = Basic Servo
  J16 = Basic Servo
  C1 = Electrolytic Capacitor [capacitance=4.3mF voltage=35V package="100 mil [THT, electrolytic]"]
  C2 = Ceramic Capacitor [capacitance=0.1mF voltage=35V package="100 mil [THT, multilayer]"]
  M1 = gy9250
  Componente2 = InvenSense MPU6050
  Componente3 = InvenSense MPU6050

nets:
  GND P: J1.gnd, Mod1.pin3#2, Mod2.pin3#2, Buck_Convertor1.Negative_Input, U1.Pin_3, R2.Pin_0, U2.Pin_3, R4.Pin_0, U3.Pin_3, U4.Pin_3, R7.Pin_0, R8.Pin_0, U5.Pin_3, U6.Pin_3, U7.Pin_3, U8.Pin_3, R13.Pin_0, R14.Pin_0, R15.Pin_0, R16.Pin_0, U9.Pin_3, U10.Pin_3, U11.Pin_3, U12.Pin_3, R21.Pin_0, R22.Pin_0, R23.Pin_0, R24.Pin_0, U13.Pin_3, U14.Pin_3, U15.Pin_3, U16.Pin_3, R29.Pin_0, R30.Pin_0, R31.Pin_0, R32.Pin_0, J2.gnd, J3.gnd, J4.gnd, J5.gnd, J6.gnd, J7.gnd, J8.gnd, J9.gnd, J10.gnd, J11.gnd, J12.gnd, J13.gnd, J14.gnd, J15.gnd, J16.gnd, C1.-, C2.0
  7.4v DC: J1.vcc, Mod1.pin3#3, Mod2.pin3#3, Buck_Convertor1.Positive_Input, R2.Pin_1, R4.Pin_1, R7.Pin_1, R8.Pin_1, R13.Pin_1, R14.Pin_1, R15.Pin_1, R16.Pin_1, R21.Pin_1, R22.Pin_1, R23.Pin_1, R24.Pin_1, R29.Pin_1, R30.Pin_1, R31.Pin_1, R32.Pin_1, J2.vcc, J3.vcc, J4.vcc, J5.vcc, J6.vcc, J7.vcc, J8.vcc, J9.vcc, J10.vcc, J11.vcc, J12.vcc, J13.vcc, J14.vcc, J15.vcc, J16.vcc, C1.+, C2.1
  Servo 1: J1.pulse, U1.Pin_4
  N1: Lipo_1s.+, Mod1.pin1
  N2: Lipo_1s.-, Mod1.pin3#4, Lipo_1s_2.+
  N3: Mod1.pin2, Lipo_1s_2.-
  N4: Lipo_1s_3.+, Mod2.pin1
  N5: Lipo_1s_3.-, Lipo_1s_4.+, Mod2.pin3#4
  N6: Lipo_1s_4.-, Mod2.pin2
  SDA: esp1.IO21, Componente1.SDA, M1.pin4
  SCL: esp1.IO22, Componente1.SCL, M1.pin3
  GND C: esp1.GND, Buck_Convertor1.Negative_Output, Componente1.GND, U1.Pin_2, U2.Pin_2, U3.Pin_2, U4.Pin_2, U5.Pin_2, U6.Pin_2, U7.Pin_2, U8.Pin_2, U9.Pin_2, U10.Pin_2, U11.Pin_2, U12.Pin_2, U13.Pin_2, U14.Pin_2, U15.Pin_2, U16.Pin_2, M1.pin2, Componente2.GND, Componente2.AD0, Componente3.GND
  3v DC: esp1.3V3, Componente1.VCC, M1.pin1, Componente2.VCC, Componente3.VCC, Componente3.AD0
  SCL 2: esp1.IO25, Componente2.SCL, Componente3.SCL
  SDA 2: esp1.IO26, Componente2.SDA, Componente3.SDA
  5v DC: esp1.5V
  5v: Buck_Convertor1.Positive_Output
  S8: Componente1.PWM7, R10.Pin_0
  S7: Componente1.PWM6, R9.Pin_0
  S6: Componente1.PWM5, R11.Pin_0
  S5: Componente1.PWM4, R12.Pin_0
  S4: Componente1.PWM3, R6.Pin_0
  S3: Componente1.PWM2, R5.Pin_0
  S2: Componente1.PWM1, R3.Pin_0
  S1: Componente1.PWM0, R1.Pin_0
  S16: Componente1.PWM15, R26.Pin_0
  S15: Componente1.PWM14, R25.Pin_0
  S14: Componente1.PWM13, R27.Pin_0
  S13: Componente1.PWM12, R28.Pin_0
  S12: Componente1.PWM11, R18.Pin_0
  S11: Componente1.PWM10, R17.Pin_0
  S10: Componente1.PWM9, R19.Pin_0
  S9: Componente1.PWM8, R20.Pin_0
  N7: U1.Pin_1, R1.Pin_1
  N8: U2.Pin_1, R3.Pin_1
  Servo 2: U2.Pin_4, J2.pulse
  N9: U3.Pin_1, R6.Pin_1
  Servo 4: U3.Pin_4, J3.pulse
  N10: U4.Pin_1, R5.Pin_1
  Servo 3: U4.Pin_4, J4.pulse
  N11: U5.Pin_1, R10.Pin_1
  Servo 8: U5.Pin_4, J7.pulse
  N12: U6.Pin_1, R12.Pin_1
  Servo 5: U6.Pin_4, J8.pulse
  N13: U7.Pin_1, R11.Pin_1
  Servo 6: U7.Pin_4, J5.pulse
  N14: U8.Pin_1, R9.Pin_1
  Servo 7: U8.Pin_4, J6.pulse
  N15: U9.Pin_1, R18.Pin_1
  Servo 12: U9.Pin_4, J13.pulse
  N16: U10.Pin_1, R20.Pin_1
  Servo 9: U10.Pin_4, J16.pulse
  N17: U11.Pin_1, R19.Pin_1
  Servo 10: U11.Pin_4, J11.pulse
  N18: U12.Pin_1, R17.Pin_1
  Servo 11: U12.Pin_4, J14.pulse
  N19: U13.Pin_1, R26.Pin_1
  Servo 16: U13.Pin_4, J9.pulse
  N20: U14.Pin_1, R28.Pin_1
  Servo 13: U14.Pin_4, J12.pulse
  N21: U15.Pin_1, R27.Pin_1
  Servo 14: U15.Pin_4, J10.pulse
  N22: U16.Pin_1, R25.Pin_1
  Servo 15: U16.Pin_4, J15.pulse

custom parts:
  LIPO-2200mAh: 2200mAh Lipo-battery
  2S-BMS: 2S-BMS LIPO battery charger / protection unit. Note pcb does not match the board as it will likely connect with wires, so pcb is 5 pads suitable for .1in header pins.
  ESP32 DevKitc V4: ESP32-DevKitC board with ESP32-WROOM-32 module. ESP32-DevKitC V4 is a small-sized ESP32-based development board produced by Espressif. Most of the pins on the ESP module are broken out to the pin headers on the board. The pins D0, D1, D2, D3, CMD and CLK are used internally for communication between ESP32 and SPI flash memory. They are grouped on both sides near the USB connector. Avoid using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
  Buck Convertor: DC to DC buck convertor
  Adafruit PCA9685 PWM/Servo Breakout: Using only two pins, control 16 free-running PWM outputs! I2C-controlled PWM driver with a built in clock. Unlike the TLC5940 family, you do not need to continuously send it signal tying up your microcontroller, its completely free running! 5V compliant, which means you can control it from a 3.3V microcontroller and still safely drive up to 6V outputs (this is good for when you want to control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
  gy9250: MPU-9250 module (three-axis gyroscope + three-axis acceleration + three-axis magnetic field). The generic model from ebay et. al. rather than the Sparkfun version.
