# Fritzing sketch Esquematico Arusha (saved by Fritzing 1.0.6)
breadboards: 2

parts:
  J3 = Basic Servo
  V3 = AC Power [voltage=5V amplitude=110V frequency=60Hz offset_voltage=0V delay_time=0s damping_factor=0s-1 phase=0degrees internal_resistance=0.1Ω]
  PS1 = prefix0000 [part_number=S-350-60]
  Buck_Convertor2 = Buck Convertor [part_number=LM2596 package=THT]
  M1 = ESP32-S3-DevKitC-1-N8R8-v1 [part_number=ESP32-S3-DevKitC-1-N8R8-v1]
  V4 = AC Power [voltage=5V amplitude=110V frequency=60Hz offset_voltage=0V delay_time=0s damping_factor=0s-1 phase=0degrees internal_resistance=0.1Ω]
  PS1_2 = prefix0000 [part_number=S-350-60]
  J4 = Basic Servo
  J5 = Basic Servo
  D1 = Schottky Diode [part_number=1N5817 package="Melf DO-213 AB [SMD]"]
  C1 = Electrolytic Capacitor [capacitance=1mF voltage=35V package="0807 [SMD, electrolytic]"]
  100_nf = Capacitor [package=cap-pth-small2]
  M2 = Stepper Motor - Bipolar
  A1 = DM860A Stepper Motor Driver
  LLC1 = Logic Level Converter [package="Breakout board"]
  A2 = XL6009E1 Boost Convertor
  1000uf_50v = Capacitor Polarized [package=cpol-radial-1000uf-63v]

nets:
  GND: J3.gnd, PS1.connector3, PS1.connector6, Buck_Convertor2.Negative_Input, Buck_Convertor2.Negative_Output, M1.pin_22, M1.pin_44, PS1_2.connector3, PS1_2.connector6, J4.gnd, J5.gnd, D1.cathode, C1.-, 100_nf.2, A1.GND, A1.ENBL-(ENB), A1.DIR-(DIR), A1.PUL-(PUL), LLC1.L-GND, LLC1.H-GND, A2.Pin_2, A2.Pin_3, 1000uf_50v.-
  12v DC: J3.vcc, PS1.connector2, Buck_Convertor2.Positive_Input, A2.Pin_1
  s1: J3.pulse, M1.pin_40
  N1: V3.V+, PS1.connector8
  N2: V3.V-, PS1.connector7
  7v DC: Buck_Convertor2.Positive_Output, J4.vcc, J5.vcc, D1.anode, C1.+, 100_nf.1
  3v DC: M1.pin_1, LLC1.LV
  5v DC: M1.pin_21, PS1_2.connector2, LLC1.HV
  s5: M1.pin_36, LLC1.LV1
  s4: M1.pin_37, LLC1.LV3
  s3: M1.pin_38, J5.pulse
  s2: M1.pin_39, J4.pulse
  N3: V4.V+, PS1_2.connector8
  N4: V4.V-, PS1_2.connector7
  N5: M2.A, A1.A+
  N6: M2.C, A1.A-
  N7: M2.B, A1.B+
  N8: M2.D, A1.B-
  N9: A1.VDC, A2.Pin_4, 1000uf_50v.+
  N10: A1.DIR+(+5V), LLC1.HV3
  N11: A1.PUL+(+5V), LLC1.HV1

notes:
  30v out

custom parts:
  Buck Convertor: DC to DC buck convertor
  ESP32-S3-DevKitC-1-N8R8-v1: ESP32-S3-DevKitC-1-N8R8-v1 This module is 44pins long (2x22) and 11 pins width.
  DM860A Stepper Motor Driver: DM860A is a type of two-phase hybrid stepping motor driver, The drive voltage of which is from 24VDC to 80VDC. It is designed for use with 2-phase hybrid stepper motor of all kinds with 57mm to 110mm outside diameter and less than 8.0A phase current. Mar 2023: Correct pcb layerId as the part won't save correctly in a .fzz file as is.
  Logic Level Converter: 5V to/from 3.3V logic level converter
  XL6009E1 Boost Convertor: The universal DC-DC converter is made on the XL6009 chip according to the Buck-Boost Converter circuit.
