# Fritzing sketch Esquematico WRO (saved by Fritzing 1.0.6)
breadboards: 2

parts:
  esp1 = ESP32 DevKitc V4
  J3 = Basic Servo
  V3 = AC Power [voltage=5V amplitude=110V frequency=60Hz offset_voltage=0V delay_time=0s damping_factor=0s-1 phase=0degrees internal_resistance=0.1Ω]
  PS1 = prefix0000 [part_number=S-350-60]
  Buck_Convertor1 = Buck Convertor [part_number=LM2596 package=THT]
  C1 = Electrolytic Capacitor [capacitance=680µF voltage=35V package="100 mil [THT, electrolytic]"]
  C2 = Ceramic Capacitor [capacitance=100nF voltage=35V package="100 mil [THT, multilayer]"]
  C3 = Ceramic Capacitor [capacitance=100nF voltage=35V package="100 mil [THT, multilayer]"]
  Componente1 = Adafruit PCA9685 PWM/Servo Breakout [part_number=815]
  U1 = Sharp PC817 [package=THT]
  R1 = Resistor [tolerance=±5% power=0.25W resistance=220 package=THT]
  R2 = Resistor [tolerance=±5% power=0.25W resistance=1k package=THT]
  U2 = Sharp PC817 [package=THT]
  R3 = Resistor [tolerance=±5% power=0.25W resistance=220 package=THT]
  R4 = Resistor [tolerance=±5% power=0.25W resistance=1k package=THT]
  U3 = Sharp PC817 [package=THT]
  U4 = Sharp PC817 [package=THT]
  R5 = Resistor [tolerance=±5% power=0.25W resistance=220 package=THT]
  R6 = Resistor [tolerance=±5% power=0.25W resistance=220 package=THT]
  R7 = Resistor [tolerance=±5% power=0.25W resistance=1k package=THT]
  R8 = Resistor [tolerance=±5% power=0.25W resistance=1k package=THT]
  J4 = Basic Servo
  J5 = Basic Servo
  J6 = Basic Servo
  Buck_Convertor2 = Buck Convertor [part_number=LM2596 package=THT]

nets:
  N1: esp1.IO21, Componente1.SDA
  N2: esp1.IO22, Componente1.SCL
  GND C: esp1.GND#18, Buck_Convertor1.Negative_Output, C3.0, Componente1.GND, U1.Pin_2, U2.Pin_2, U3.Pin_2, U4.Pin_2
  3v DC: esp1.3V3, C3.1, Componente1.VCC
  5v DC: esp1.5V, Buck_Convertor1.Positive_Output, Componente1.5.0V
  GND P: J3.gnd, PS1.connector3, Buck_Convertor1.Negative_Input, C1.-, C2.0, U1.Pin_3, R2.Pin_0, U2.Pin_3, R4.Pin_0, U3.Pin_3, U4.Pin_3, R7.Pin_0, R8.Pin_0, J4.gnd, J5.gnd, J6.gnd, Buck_Convertor2.Negative_Input, Buck_Convertor2.Negative_Output
  12v DC: J3.vcc, PS1.connector1, Buck_Convertor1.Positive_Input, C1.+, C2.1, R2.Pin_1, R4.Pin_1, R7.Pin_1, R8.Pin_1, J4.vcc, Buck_Convertor2.Positive_Input
  N3: J3.pulse, U1.Pin_4
  N4: V3.V+, PS1.connector8
  N5: V3.V-, PS1.connector7
  GND: PS1.connector6
  S4: Componente1.PWM3, R6.Pin_0
  S3: Componente1.PWM2, R5.Pin_0
  S2: Componente1.PWM1, R3.Pin_0
  S1: Componente1.PWM0, R1.Pin_0
  N6: U1.Pin_1, R1.Pin_1
  N7: U2.Pin_1, R3.Pin_1
  N8: U2.Pin_4, J4.pulse
  N9: U3.Pin_1, R5.Pin_1
  N10: U3.Pin_4, J5.pulse
  N11: U4.Pin_1, R6.Pin_1
  N12: U4.Pin_4, J6.pulse
  7v DC: J5.vcc, J6.vcc, Buck_Convertor2.Positive_Output

notes:
  Fuente 110v AC
  Fuente 12v DC
  Step down 5v DC

custom parts:
  ESP32 DevKitc V4: ESP32-DevKitC board with ESP32-WROOM-32 module. ESP32-DevKitC V4 is a small-sized ESP32-based development board produced by Espressif. Most of the pins on the ESP module are broken out to the pin headers on the board. The pins D0, D1, D2, D3, CMD and CLK are used internally for communication between ESP32 and SPI flash memory. They are grouped on both sides near the USB connector. Avoid using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
  Buck Convertor: DC to DC buck convertor
  Adafruit PCA9685 PWM/Servo Breakout: Using only two pins, control 16 free-running PWM outputs! I2C-controlled PWM driver with a built in clock. Unlike the TLC5940 family, you do not need to continuously send it signal tying up your microcontroller, its completely free running! 5V compliant, which means you can control it from a 3.3V microcontroller and still safely drive up to 6V outputs (this is good for when you want to control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
