# Fritzing sketch Esquematico (saved by Fritzing 1.0.6)
breadboards: 1

parts:
  U1 = LIPO-110mAh [package=lipo-110]
  U2 = LIPO-110mAh [package=lipo-110]
  U3 = LIPO-110mAh [package=lipo-110]
  U4 = LIPO-110mAh [package=lipo-110]
  U5 = LIPO-110mAh [package=lipo-110]
  U6 = LIPO-110mAh [package=lipo-110]
  U7 = LIPO-110mAh [package=lipo-110]
  U8 = LIPO-110mAh [package=lipo-110]
  U9 = LIPO-110mAh [package=lipo-110]
  U10 = LIPO-110mAh [package=lipo-110]
  S1 = Square Pushbutton
  U11 = LuaNode32 / ESP32 [part_number=ESP32]
  Temperatura_ambiente_y_presion = BME280
  Temperatura_agua = DS18B20 1-Wire Temperature Sensor Probe
  R1 = Resistor [tolerance=±5% power=0.25W resistance=4.7k package=THT]
  GPS = u-blox NEO-6M GPS Breakout
  R2 = Resistor [tolerance=±5% power=0.25W resistance=1k package=THT]
  Q1 = NPN-Transistor [package="TO92 [THT]"]
  R3 = Resistor [tolerance=±5% power=0.25W resistance=1k package=THT]
  Q2 = NPN-Transistor [package="TO92 [THT]"]
  Pareja_de_elctrodos_1 = Header 2 [package=jst-2-pth]
  Pareja_de_electrodos_2 = Header 2 [package=jst-2-pth]
  R4 = Resistor [tolerance=±5% resistance=2.2k package="0805 [SMD]"]
  R5 = Resistor [tolerance=±5% resistance=2.2k package="0805 [SMD]"]
  Arduino = Arduino Nano (Rev3.0) (ICSP)
  Distancia = HC-SR04 Ultrasonic Distance Sensor
  Distancia_2 = HC-SR04 Ultrasonic Distance Sensor
  Distancia_3 = HC-SR04 Ultrasonic Distance Sensor
  Mod1 = ESP32 - CAM
  J1 = Basic Servo
  U17 = LuaNode32 / ESP32 [part_number="ESP32 F"]
  HC-SR04_Sensor_1 = HC-SR04 Ultrasonic Distance Sensor
  R6 = Resistor [tolerance=±5% power=0.25W resistance=100k package=THT]
  R7 = Resistor [tolerance=±5% power=0.25W resistance=10k package=THT]
  Q3 = NPN-Transistor [package="TO92 [THT]"]
  Q5 = Basic FET N-Channel [package="DPak [SMD]"]
  R8 = Resistor [tolerance=±5% power=0.25W resistance=47 package=THT]
  U14 = LIPO-110mAh [package=lipo-110]
  U15 = LIPO-110mAh [package=lipo-110]
  MOD1 = MT3608/B6289 Boost Module
  U16 = LM2596 step down module
  R9 = Resistor [tolerance=±5% power=0.25W resistance=1k package=THT]
  R10 = Resistor [tolerance=±5% power=0.25W resistance=1k package=THT]
  J2 = Piezo Speaker
  Q6 = NPN-Transistor [package="TO92 [THT]"]
  Q7 = Basic FET N-Channel [package="DPak [SMD]"]
  R11 = Resistor [tolerance=±5% power=0.25W resistance=47 package=THT]
  R12 = Resistor [tolerance=±5% power=0.25W resistance=1k package=THT]
  R13 = Resistor [tolerance=±5% power=0.25W resistance=1k package=THT]
  LED1 = LED - 3mm [color="Red (633nm)" current=0.030A package="3 mm [THT]"]
  R15 = Resistor [tolerance=±5% power=0.25W resistance=10k package=THT]
  R16 = Resistor [tolerance=±5% power=0.25W resistance=1k package=THT]
  R17 = Resistor [tolerance=±5% power=0.25W resistance=10k package=THT]
  R18 = Resistor [tolerance=±5% power=0.25W resistance=1k package=THT]
  S2 = Square Pushbutton
  DC1 = DC_DC_XL4016 [package=board_screw]
  A1 = drv-1012
  M1 = gear-motor
  R19 = Photocell (LDR) [power=0.25W dark_resistance_@0.01lx=300kΩ light_resistance_@100lx=400Ω luminance=10lx package=THT]
  R20 = Resistor [tolerance=±5% resistance=10k package="0805 [SMD]"]
  LED2 = LED - 5mm [color="Red (633nm)" current=0.030A package="5 mm [THT]"]
  R21 = Resistor [tolerance=±5% power=0.25W resistance=220 package=THT]
  R22 = Resistor [tolerance=±5% power=0.25W resistance=2.2k package=THT]  # not connected
  R23 = Resistor [tolerance=±5% power=0.25W resistance=10k package=THT]

nets:
  N1: U1.+, U2.-
  GND: U1.-, U7.-, U11.GND, Temperatura_ambiente_y_presion.GND, Temperatura_agua.GND, GPS.Pin_2, Q2.E, R5.Pin_1, Arduino.GND, Distancia.GND, Distancia_2.GND, Distancia_3.GND, Mod1.GND, J1.gnd, Q3.E, Q6.E, R15.Pin_0, R17.Pin_0, DC1.IN-, DC1.OUT-, A1.Pin_1, A1.Pin_9, R20.Pin_1, LED2.cathode
  N2: U2.+, U3.-
  N3: U3.+, U4.-
  N4: U4.+, U5.-
  N5: U5.+, U9.+, S1.leg0
  N6: U6.+, U10.-
  N7: U6.-, U8.+
  N8: U7.+, U8.-
  N9: U9.-, U10.+
  20v: S1.leg1, DC1.IN+, A1.Pin_10
  N10: U11.D34, Pareja_de_elctrodos_1.2
  N11: U11.D35, Pareja_de_electrodos_2.2
  N12: U11.D14, R2.Pin_0
  N13: U11.D13, R3.Pin_0
  5v: U11.Vin, Arduino.5V, Distancia.VCC, Distancia_2.VCC, Distancia_3.VCC, Mod1.5V, J1.vcc, DC1.OUT+, A1.Pin_3, A1.Pin_5, A1.Pin_7, R19.pin_0
  3.3v: U11.3V3, Temperatura_ambiente_y_presion.VIN, Temperatura_agua.VDD, R1.Pin_0, GPS.Pin_1, Q1.C, R4.Pin_0
  N14: U11.RX2, GPS.Pin_3
  N15: U11.D5, Temperatura_agua.DQ, R1.Pin_1
  N16: U11.D21, Temperatura_ambiente_y_presion.SDA
  N17: R2.Pin_1, Q1.B
  N18: Q1.E, Q2.C, Pareja_de_elctrodos_1.1
  N19: R3.Pin_1, Q2.B
  N20: Pareja_de_electrodos_2.1, R4.Pin_1, R5.Pin_0
  N21: Arduino.D2, Distancia_3.TRIG
  N22: Arduino.D3, Distancia_3.ECHO
  N23: Arduino.D4, Distancia_2.TRIG
  N24: Arduino.D5, Distancia_2.ECHO
  N25: Arduino.D6, Distancia.TRIG
  N26: Arduino.D7, Distancia.ECHO
  N27: Arduino.D8, J1.pulse
  N28: Arduino.D9, A1.Pin_8
  N29: Arduino.D10, A1.Pin_4
  N30: Arduino.D11/MOSI, R21.Pin_1
  N31: Arduino.A7, R19.pin_1, R20.Pin_0
  N32: U17.D26, R6.Pin_1, R23.Pin_0
  N33: U17.D27, HC-SR04_Sensor_1.TRIG
  GND F: U17.GND, HC-SR04_Sensor_1.GND, R7.Pin_1, Q5.source, U15.-, MOD1.IN_(-), MOD1.OUT_(-), U16.IN-, U16.OUT-, R10.Pin_1, Q7.source, R13.Pin_1
  5v F: U17.Vin, HC-SR04_Sensor_1.VCC, U16.OUT+, LED1.anode
  N34: U17.D18, R15.Pin_1, R16.Pin_0
  N35: U17.D19, R17.Pin_1, R18.Pin_0
  N36: HC-SR04_Sensor_1.ECHO, R6.Pin_0
  N37: R7.Pin_0, R23.Pin_1
  N38: Q3.B, R16.Pin_1
  N39: Q3.C, R8.Pin_0, R9.Pin_1, R10.Pin_0
  N40: Q5.Gate, R8.Pin_1
  N41: Q5.drain, J2.pin1
  N42: U14.+, S2.leg0
  N43: U14.-, U15.+
  N44: MOD1.IN_(+), S2.leg1
  24v F: MOD1.OUT_(+), U16.IN+, R9.Pin_0, J2.pin2, R12.Pin_0
  N45: Q6.B, R18.Pin_1
  N46: Q6.C, R11.Pin_0, R12.Pin_1, R13.Pin_0
  N47: Q7.Gate, R11.Pin_1
  N48: Q7.drain, LED1.cathode
  N49: A1.Pin_11, M1.pin_2
  N50: A1.Pin_12, M1.pin_1
  N51: LED2.anode, R21.Pin_0

notes:
  ESP32 Catamorán
  Arduino nano Catamorán
  ESP32 cam Catamorán
  Farol

custom parts:
  LuaNode32 / ESP32: New Image for LuaNode32 DOIT ESP32 DEVKIT V1. Base parts from LuaNode32 / ESP32 ESP32 based LuaNode32 by G.Noorlander DOIT Esp32 DevKit v1 (30 pins long, 11 pins width) by Werner Rothschopf (modified by vanepp Dec 2018)
  BME280: Temperature Humidity Barometric presure Sensor
  ESP32 - CAM: The ESP32-CAM has a very competitive small-size camera module that can operate independently as a minimum system with a footprint of only 27*40.5*4.5mm and a deep sleep current of up to 6mA.
  MT3608/B6289 Boost Module: Chip- MT3608 / B6289 DC to DC step up, power booster module. With adjustable output voltage. Current- 2A . || Input voltage- 2V-24V || Output voltage- 5V-28V Input interface- MICRO USB || Inversed polarity- NO. || Led indicator- No.
  LM2596 step down module: LM2596 DC-DC step down power supply module 3 A.
  drv-1012: .The BTS7960 is a fully integrated high current H bridge module for motor drive applications.
