# Fritzing sketch Esquematico Joroi (saved by Fritzing 1.0.6)
# 18650 Li-ion Battery: CC-BY Dr Kristofer Chan, King's College London/Remote-research.org
breadboards: 1

parts:
  esp1 = ESP32 DevKitc V4
  A1 = j5019
  BAT1 = 18650 Li-ion Battery [package=battery-18650]
  Componente1 = Adafruit PCA9685 PWM/Servo Breakout [part_number=815]
  R1 = Resistor [tolerance=±5% power=0.25W resistance=220 package=THT]
  R2 = Resistor [tolerance=±5% power=0.25W resistance=220 package=THT]
  R3 = Resistor [tolerance=±5% power=0.25W resistance=220 package=THT]
  R4 = Resistor [tolerance=±5% power=0.25W resistance=220 package=THT]
  R5 = Resistor [tolerance=±5% power=0.25W resistance=220 package=THT]
  R6 = Resistor [tolerance=±5% power=0.25W resistance=220 package=THT]
  R7 = Resistor [tolerance=±5% power=0.25W resistance=220 package=THT]
  R8 = Resistor [tolerance=±5% power=0.25W resistance=220 package=THT]
  R9 = Resistor [tolerance=±5% power=0.25W resistance=220 package=THT]
  LED1 = LEDs [package=led10mm]
  LED2 = LEDs [package=led10mm]
  LED3 = LEDs [package=led10mm]
  LED4 = LEDs [package=led10mm]
  LED5 = LEDs [package=led10mm]
  LED6 = LEDs [package=led10mm]
  LED7 = LEDs [package=led10mm]
  LED8 = LEDs [package=led10mm]
  LED9 = LEDs [package=led10mm]
  Sensor_touch_1 = TEST-POINT [package=pad.03x.03]
  Sensor_touch_2 = TEST-POINT [package=pad.03x.03]
  Sensor_touch_3 = TEST-POINT [package=pad.03x.03]
  Sensor_touch_4 = TEST-POINT [package=pad.03x.03]
  Sensor_touch_5 = TEST-POINT [package=pad.03x.03]
  Sensor_touch_6 = TEST-POINT [package=pad.03x.03]
  Sensor_touch_7 = TEST-POINT [package=pad.03x.03]
  Sensor_touch_8 = TEST-POINT [package=pad.03x.03]
  R10 = Resistor [tolerance=±5% power=0.25W resistance=1M package=THT]
  Pin_de_descarga_(espera) = TEST-POINT [package=pad.03x.03]
  Part1 = KY-037 High Sensitivity Sound Detection Module [package="Breakout board"]

nets:
  N1: esp1.IO15, Sensor_touch_8.1
  N2: esp1.IO2, Sensor_touch_7.1
  N3: esp1.IO4, Sensor_touch_5.1
  N4: esp1.IO21, Componente1.SDA
  N5: esp1.IO22, Componente1.SCL
  GND: esp1.GND, A1.Pin_2, A1.Pin_5, BAT1.-, Componente1.GND, LED1.C, LED2.C, LED3.C, LED4.C, LED5.C, LED6.C, LED7.C, LED8.C, LED9.C, R10.Pin_1, Part1.G
  N6: esp1.IO32, Sensor_touch_1.1
  N7: esp1.IO33, Sensor_touch_2.1
  N8: esp1.IO25, Part1.A0
  N9: esp1.IO27, Sensor_touch_3.1
  N10: esp1.IO14, Sensor_touch_4.1
  N11: esp1.IO13, Sensor_touch_6.1
  5v: esp1.5V, A1.Pin_1, Componente1.5.0V, Componente1.VCC, Part1.+
  N12: A1.Pin_6, BAT1.+
  N13: Componente1.PWM7, R8.Pin_0
  N14: Componente1.PWM6, R7.Pin_0
  N15: Componente1.PWM5, R6.Pin_0
  N16: Componente1.PWM4, R5.Pin_0
  N17: Componente1.PWM3, R4.Pin_0
  N18: Componente1.PWM2, R3.Pin_0
  N19: Componente1.PWM1, R2.Pin_0
  N20: Componente1.PWM0, R1.Pin_0
  N21: Componente1.PWM8, R9.Pin_0
  N22: R1.Pin_1, LED1.A
  N23: R2.Pin_1, LED2.A
  N24: R3.Pin_1, LED3.A
  N25: R4.Pin_1, LED4.A
  N26: R5.Pin_1, LED5.A
  N27: R6.Pin_1, LED6.A
  N28: R7.Pin_1, LED7.A
  N29: R8.Pin_1, LED8.A
  N30: R9.Pin_1, LED9.A
  N31: R10.Pin_0, Pin_de_descarga_(espera).1

custom parts:
  ESP32 DevKitc V4: ESP32-DevKitC board with ESP32-WROOM-32 module. ESP32-DevKitC V4 is a small-sized ESP32-based development board produced by Espressif. Most of the pins on the ESP module are broken out to the pin headers on the board. The pins D0, D1, D2, D3, CMD and CLK are used internally for communication between ESP32 and SPI flash memory. They are grouped on both sides near the USB connector. Avoid using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
  j5019: This module is a small single cell lithium battery charging module which also includes a 1A step-up (boost) converter for powering a large range of applications.
  18650 Li-ion Battery: 18650 li-ion Battery Standard 18650 battery with interactive connectors Creative Common Attribution 4.0 International (CC-BY 4.0) license. Any use of this part requires attribution of Dr Kristofer Chan, Department of Geography, King's College London. Contact kristofer.chan [at] kcl.ac.uk OR kris [at] remote-research.org for further information.
  Adafruit PCA9685 PWM/Servo Breakout: Using only two pins, control 16 free-running PWM outputs! I2C-controlled PWM driver with a built in clock. Unlike the TLC5940 family, you do not need to continuously send it signal tying up your microcontroller, its completely free running! 5V compliant, which means you can control it from a 3.3V microcontroller and still safely drive up to 6V outputs (this is good for when you want to control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
  KY-037 High Sensitivity Sound Detection Module: KY-037 high sensitivity sound detection module is an analog/digital sensor that uses a condenser microphone to observe changes in environment noise.
