# Fritzing sketch Esquematico Apiña (saved by Fritzing 1.0.6)
breadboards: 1

parts:
  PS1 = prefix0000 [part_number=S-350-60]
  V1 = AC Power [voltage=0]
  IR1 = TSOP312.., 314.. [package=THT]
  LED1 = LED - 5mm [color="Infrared (850nm)" current=0.030A package="5 mm [THT]"]
  U1 = WS2812 RGB LED strip
  J2 = USB type C-05-power-only
  M1 = ESP32-S3-DevKitC-1-N8R8-v1 [part_number=ESP32-S3-DevKitC-1-N8R8-v1]
  Componente1 = Arduino Uno (Rev3)
  Q1 = NPN-Transistor [package="TO92 [THT]"]
  R1 = Resistor [tolerance=±5% power=0.25W resistance=1k package=THT]
  PS1_2 = prefix0000 [part_number=S-350-60]
  V2 = AC Power [voltage=0]
  R2 = Resistor [tolerance=±5% power=0.25W resistance=22 package=THT]

nets:
  5v: PS1.connector2, J2.Pin_2, Componente1.5V, R2.Pin_0
  GND: PS1.connector3, PS1.connector6, IR1.GND, U1.GND, J2.Pin_3, Componente1.GND, Q1.E, PS1_2.connector3, PS1_2.connector6
  N1: PS1.connector7, V1.V-
  N2: PS1.connector8, V1.V+
  12v: IR1.Vs, U1.VCC, PS1_2.connector2
  N3: IR1.Data, U1.DIN
  N4: LED1.cathode, Q1.C
  N5: LED1.anode, R2.Pin_1
  N6: J2.Pin_1, J2.Pin_4, M1.pin_21, M1.pin_22, M1.pin_23
  N7: M1.pin_43, Componente1.D0/RX
  N8: Componente1.D4, R1.Pin_0
  N9: Q1.B, R1.Pin_1
  N10: PS1_2.connector7, V2.V-
  N11: PS1_2.connector8, V2.V+

custom parts:
  AC Power: A generic ac power symbol
  WS2812 RGB LED strip: WS2812 strip
  ESP32-S3-DevKitC-1-N8R8-v1: ESP32-S3-DevKitC-1-N8R8-v1 This module is 44pins long (2x22) and 11 pins width.
