# Fritzing sketch Esquematico Arusha (saved by Fritzing 1.0.6)
breadboards: 1

parts:
  Componente3 = Arduino Uno (Rev3)
  LED2 = LED - 5mm [color="Infrared (940nm)" current=0.030A package="5 mm [THT]"]
  Q2 = NPN-Transistor [package="TO92 [THT]"]
  R3 = Resistor [tolerance=±5% power=0.25W resistance=22 package=THT]
  R4 = Resistor [tolerance=±5% power=0.25W resistance=1k package=THT]
  Componente4 = Adafruit FTDI Friend [part_number="Adafruit #284"]
  M5 = ESP32-S3-DevKitC-1-N8R8-v1 [part_number=ESP32-S3-DevKitC-1-N8R8-v1]
  M6 = ESP32-S3-DevKitC-1-N8R8-v1 [part_number=ESP32-S3-DevKitC-1-N8R8-v1]
  D2 = Schottky Diode [part_number=1N5817 package="Melf DO-213 AB [SMD]"]
  C2 = Electrolytic Capacitor [capacitance=1mF voltage=35V package="0807 [SMD, electrolytic]"]
  100_nf1 = Capacitor [package=cap-pth-small2]
  J7 = Basic Servo
  J8 = Basic Servo
  V5 = AC Power [voltage=5V amplitude=110V frequency=60Hz offset_voltage=0V delay_time=0s damping_factor=0s-1 phase=0degrees internal_resistance=0.1Ω]
  V6 = AC Power [voltage=5V amplitude=110V frequency=60Hz offset_voltage=0V delay_time=0s damping_factor=0s-1 phase=0degrees internal_resistance=0.1Ω]
  PS1 = prefix0000 [part_number=S-350-60]
  PS1_2 = prefix0000 [part_number=S-350-60]
  Buck_Convertor3 = Buck Convertor [part_number=LM2596 package=THT]
  L9 = Solenoid
  Q13 = Basic FET N-Channel [package="TO220 [THT]"]
  R20 = Resistor [tolerance=±5% power=0.25W resistance=47 package=THT]
  Componente5 = Adafruit PCA9685 PWM/Servo Breakout [part_number=815]
  Q14 = TRANSISTOR_NPN [package=to-92-ammo]
  R26 = Resistor [tolerance=±5% power=0.25W resistance=1k package=THT]
  D11 = Schottky Diode [part_number=1N5817 package="Melf DO-213 AB [SMD]"]
  R27 = Resistor [tolerance=±5% power=0.25W resistance=2.2k package=THT]
  L10 = Solenoid
  Q15 = Basic FET N-Channel [package="TO220 [THT]"]
  R28 = Resistor [tolerance=±5% power=0.25W resistance=47 package=THT]
  Q16 = TRANSISTOR_NPN [package=to-92-ammo]
  R29 = Resistor [tolerance=±5% power=0.25W resistance=1k package=THT]
  D12 = Schottky Diode [part_number=1N5817 package="Melf DO-213 AB [SMD]"]
  R30 = Resistor [tolerance=±5% power=0.25W resistance=2.2k package=THT]
  L11 = Solenoid
  L12 = Solenoid
  Q17 = Basic FET N-Channel [package="TO220 [THT]"]
  Q18 = Basic FET N-Channel [package="TO220 [THT]"]
  R31 = Resistor [tolerance=±5% power=0.25W resistance=47 package=THT]
  R32 = Resistor [tolerance=±5% power=0.25W resistance=47 package=THT]
  Q19 = TRANSISTOR_NPN [package=to-92-ammo]
  Q20 = TRANSISTOR_NPN [package=to-92-ammo]
  R33 = Resistor [tolerance=±5% power=0.25W resistance=1k package=THT]
  R34 = Resistor [tolerance=±5% power=0.25W resistance=1k package=THT]
  D13 = Schottky Diode [part_number=1N5817 package="Melf DO-213 AB [SMD]"]
  D14 = Schottky Diode [part_number=1N5817 package="Melf DO-213 AB [SMD]"]
  R35 = Resistor [tolerance=±5% power=0.25W resistance=2.2k package=THT]
  R36 = Resistor [tolerance=±5% power=0.25W resistance=2.2k package=THT]
  L13 = Solenoid
  L14 = Solenoid
  L15 = Solenoid
  L16 = Solenoid
  Q21 = Basic FET N-Channel [package="TO220 [THT]"]
  Q22 = Basic FET N-Channel [package="TO220 [THT]"]
  Q23 = Basic FET N-Channel [package="TO220 [THT]"]
  Q24 = Basic FET N-Channel [package="TO220 [THT]"]
  R37 = Resistor [tolerance=±5% power=0.25W resistance=47 package=THT]
  R38 = Resistor [tolerance=±5% power=0.25W resistance=47 package=THT]
  R39 = Resistor [tolerance=±5% power=0.25W resistance=47 package=THT]
  R40 = Resistor [tolerance=±5% power=0.25W resistance=47 package=THT]
  Q25 = TRANSISTOR_NPN [package=to-92-ammo]
  Q26 = TRANSISTOR_NPN [package=to-92-ammo]
  Q27 = TRANSISTOR_NPN [package=to-92-ammo]
  Q28 = TRANSISTOR_NPN [package=to-92-ammo]
  R41 = Resistor [tolerance=±5% power=0.25W resistance=1k package=THT]
  R42 = Resistor [tolerance=±5% power=0.25W resistance=1k package=THT]
  R43 = Resistor [tolerance=±5% power=0.25W resistance=1k package=THT]
  R44 = Resistor [tolerance=±5% power=0.25W resistance=1k package=THT]
  D15 = Schottky Diode [part_number=1N5817 package="Melf DO-213 AB [SMD]"]
  D16 = Schottky Diode [part_number=1N5817 package="Melf DO-213 AB [SMD]"]
  D17 = Schottky Diode [part_number=1N5817 package="Melf DO-213 AB [SMD]"]
  R45 = Resistor [tolerance=±5% power=0.25W resistance=2.2k package=THT]
  R46 = Resistor [tolerance=±5% power=0.25W resistance=2.2k package=THT]
  R47 = Resistor [tolerance=±5% power=0.25W resistance=2.2k package=THT]
  R48 = Resistor [tolerance=±5% power=0.25W resistance=2.2k package=THT]
  L17 = Solenoid
  L18 = Solenoid
  L19 = Solenoid
  L20 = Solenoid
  Q29 = Basic FET N-Channel [package="TO220 [THT]"]
  Q30 = Basic FET N-Channel [package="TO220 [THT]"]
  Q31 = Basic FET N-Channel [package="TO220 [THT]"]
  Q32 = Basic FET N-Channel [package="TO220 [THT]"]
  R49 = Resistor [tolerance=±5% power=0.25W resistance=47 package=THT]
  R50 = Resistor [tolerance=±5% power=0.25W resistance=47 package=THT]
  R51 = Resistor [tolerance=±5% power=0.25W resistance=47 package=THT]
  R52 = Resistor [tolerance=±5% power=0.25W resistance=47 package=THT]
  Q33 = TRANSISTOR_NPN [package=to-92-ammo]
  Q34 = TRANSISTOR_NPN [package=to-92-ammo]
  Q35 = TRANSISTOR_NPN [package=to-92-ammo]
  Q36 = TRANSISTOR_NPN [package=to-92-ammo]
  R53 = Resistor [tolerance=±5% power=0.25W resistance=1k package=THT]
  R54 = Resistor [tolerance=±5% power=0.25W resistance=1k package=THT]
  R55 = Resistor [tolerance=±5% power=0.25W resistance=1k package=THT]
  R56 = Resistor [tolerance=±5% power=0.25W resistance=1k package=THT]
  D19 = Schottky Diode [part_number=1N5817 package="Melf DO-213 AB [SMD]"]
  D20 = Schottky Diode [part_number=1N5817 package="Melf DO-213 AB [SMD]"]
  D21 = Schottky Diode [part_number=1N5817 package="Melf DO-213 AB [SMD]"]
  D22 = Schottky Diode [part_number=1N5817 package="Melf DO-213 AB [SMD]"]
  R57 = Resistor [tolerance=±5% power=0.25W resistance=2.2k package=THT]
  R58 = Resistor [tolerance=±5% power=0.25W resistance=2.2k package=THT]
  R59 = Resistor [tolerance=±5% power=0.25W resistance=2.2k package=THT]
  R60 = Resistor [tolerance=±5% power=0.25W resistance=2.2k package=THT]
  D18 = Schottky Diode [part_number=1N5817 breakdown_voltage=3.6V package="Melf DO-213 AB [SMD]"]

nets:
  Tx 1: Componente3.D0/RX, M5.pin_39
  N1: Componente3.D3_PWM, R4.Pin_0
  5v DC: Componente3.5V, R3.Pin_0, Componente4.VCC, M5.pin_21, M6.pin_21, PS1.connector2, Componente5.5.0V
  N2: LED2.cathode, Q2.C
  N3: LED2.anode, R3.Pin_1
  GND: Q2.E, Componente4.GND, M5.pin_22, M5.pin_23, M6.pin_22, M6.pin_24, M6.pin_44, D2.cathode, C2.-, 100_nf1.2, J7.gnd, J8.gnd, PS1.connector3, PS1.connector6, PS1_2.connector3, PS1_2.connector6, Buck_Convertor3.Negative_Input, Buck_Convertor3.Negative_Output, Q13.source, Componente5.GND, Q14.E, Q15.source, Q16.E, Q17.source, Q18.source, Q19.E, Q20.E, Q21.source, Q22.source, Q23.source, Q24.source, Q25.E, Q26.E, Q27.E, Q28.E, Q29.source, Q30.source, Q31.source, Q32.source, Q33.E, Q34.E, Q35.E, Q36.E
  N4: Q2.B, R4.Pin_1
  Rx: Componente4.TX, M5.pin_42
  Tx: Componente4.RX, M5.pin_43
  3v DC: M5.pin_1, M5.pin_2, M6.pin_1
  SDA: M6.pin_12, Componente5.SDA
  SCL: M6.pin_15, Componente5.SCL
  s2: M6.pin_39, J7.pulse
  s1: M6.pin_40, J8.pulse
  7v DC: D2.anode, C2.+, 100_nf1.1, J7.vcc, Buck_Convertor3.Positive_Output
  12v DC: J8.vcc, PS1_2.connector2, Buck_Convertor3.Positive_Input, L9.pin1, D11.cathode, R27.Pin_0, L10.pin1, D12.cathode, R30.Pin_0, L11.pin1, L12.pin1, D13.cathode, D14.cathode, R35.Pin_0, R36.Pin_0, L13.pin1, L14.pin1, L15.pin1, L16.pin1, D15.cathode, D16.cathode, D17.cathode, R45.Pin_0, R46.Pin_0, R47.Pin_0, R48.Pin_0, L17.pin1, L18.pin1, L19.pin1, L20.pin1, D19.cathode, D20.cathode, D21.cathode, D22.cathode, R57.Pin_0, R58.Pin_0, R59.Pin_0, R60.Pin_0, D18.cathode
  N5: V5.V+, PS1.connector8
  N6: V5.V-, PS1.connector7
  N7: V6.V+, PS1_2.connector8
  N8: V6.V-, PS1_2.connector7
  N9: L9.pin2, Q13.drain, D11.anode
  N10: Q13.gate, R20.Pin_1, R27.Pin_1
  N11: R20.Pin_0, Q14.C
  s10: Componente5.PWM7, R44.Pin_0
  s9: Componente5.PWM6, R43.Pin_0
  s8: Componente5.PWM5, R42.Pin_0
  s7: Componente5.PWM4, R41.Pin_0
  s6: Componente5.PWM3, R34.Pin_0
  s5: Componente5.PWM2, R33.Pin_0
  s4: Componente5.PWM1, R29.Pin_0
  s3: Componente5.PWM0, R26.Pin_0
  s14: Componente5.PWM11, R56.Pin_0
  s13: Componente5.PWM10, R55.Pin_0
  s12: Componente5.PWM9, R54.Pin_0
  s11: Componente5.PWM8, R53.Pin_0
  N12: Q14.B, R26.Pin_1
  N13: L10.pin2, Q15.drain, D12.anode
  N14: Q15.gate, R28.Pin_1, R30.Pin_1
  N15: R28.Pin_0, Q16.C
  N16: Q16.B, R29.Pin_1
  N17: L11.pin2, Q17.drain, D13.anode
  N18: L12.pin2, Q18.drain, D14.anode
  N19: Q17.gate, R31.Pin_1, R35.Pin_1
  N20: Q18.gate, R32.Pin_1, R36.Pin_1
  N21: R31.Pin_0, Q19.C
  N22: R32.Pin_0, Q20.C
  N23: Q19.B, R33.Pin_1
  N24: Q20.B, R34.Pin_1
  N25: L13.pin2, Q21.drain, D15.anode
  N26: L14.pin2, Q24.drain, D18.anode
  N27: L15.pin2, Q23.drain, D16.anode
  N28: L16.pin2, Q22.drain, D17.anode
  N29: Q21.gate, R37.Pin_1, R45.Pin_1
  N30: Q22.gate, R39.Pin_1, R47.Pin_1
  N31: Q23.gate, R38.Pin_1, R46.Pin_1
  N32: Q24.gate, R40.Pin_1, R48.Pin_1
  N33: R37.Pin_0, Q25.C
  N34: R38.Pin_0, Q28.C
  N35: R39.Pin_0, Q26.C
  N36: R40.Pin_0, Q27.C
  N37: Q25.B, R41.Pin_1
  N38: Q26.B, R44.Pin_1
  N39: Q27.B, R43.Pin_1
  N40: Q28.B, R42.Pin_1
  N41: L17.pin2, Q29.drain, D19.anode
  N42: L18.pin2, Q32.drain, D22.anode
  N43: L19.pin2, Q31.drain, D20.anode
  N44: L20.pin2, Q30.drain, D21.anode
  N45: Q29.gate, R49.Pin_1, R57.Pin_1
  N46: Q30.gate, R51.Pin_1, R59.Pin_1
  N47: Q31.gate, R50.Pin_1, R58.Pin_1
  N48: Q32.gate, R52.Pin_1, R60.Pin_1
  N49: R49.Pin_0, Q33.C
  N50: R50.Pin_0, Q36.C
  N51: R51.Pin_0, Q34.C
  N52: R52.Pin_0, Q35.C
  N53: Q33.B, R53.Pin_1
  N54: Q34.B, R56.Pin_1
  N55: Q35.B, R55.Pin_1
  N56: Q36.B, R54.Pin_1

custom parts:
  Adafruit FTDI Friend: Long gone are the days of parallel ports and serial ports. Now the USB port reigns supreme! But USB is hard, and you just want to transfer your every-day serial data from a microcontroller to computer. What now? Enter the FTDI Friend! The FTDI Friend is a tweaked out FTDI FT232RL chip adapter. Sure, like the well-known FTDI cable, it can provide power to your project and there are 4 signal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
  ESP32-S3-DevKitC-1-N8R8-v1: ESP32-S3-DevKitC-1-N8R8-v1 This module is 44pins long (2x22) and 11 pins width.
  Buck Convertor: DC to DC buck convertor
  Adafruit PCA9685 PWM/Servo Breakout: Using only two pins, control 16 free-running PWM outputs! I2C-controlled PWM driver with a built in clock. Unlike the TLC5940 family, you do not need to continuously send it signal tying up your microcontroller, its completely free running! 5V compliant, which means you can control it from a 3.3V microcontroller and still safely drive up to 6V outputs (this is good for when you want to control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
